# Fritzing sketch htmaa (saved by Fritzing 0.9.3b)
breadboards: 1

parts:
  Part1 = Arduino Uno (Rev3)
  C1 = Electrolytic Capacitor [capacitance=0.1mF package="100 mil [THT, electrolytic]"]
  LED1 = LED - 5mm [color="Blue (470nm)" package="5 mm [THT]"]  # not connected
  R1 = Resistor [tolerance=±5% resistance=330 package=THT]
  J1 = Basic Servo
  S1 = Pushbutton [package="[THT]"]
  R2 = Resistor [tolerance=±5% resistance=10k package=THT]
  LED2 = LED - 5mm [color="Red (633nm)" package="5 mm [THT]"]
  R3 = Resistor [tolerance=±5% resistance=330 package=THT]
  LED3 = LED - 5mm [color="Green (555nm)" package="5 mm [THT]"]
  R4 = Resistor [tolerance=±5% resistance=330 package=THT]

nets:
  N1: Part1.D9_PWM, J1.pulse
  N2: Part1.D2, S1.Pin_3, S1.Pin_4, R2.Pin_1
  N3: Part1.D5_PWM, R1.Pin_0
  N4: Part1.D6_PWM, R3.Pin_1
  N5: Part1.D7, R4.Pin_1
  N6: Part1.5V, C1.+, S1.Pin_1, S1.Pin_2
  N7: Part1.GND, C1.-, R2.Pin_0, LED2.cathode, LED3.cathode
  N8: LED2.anode, R3.Pin_0
  N9: LED3.anode, R4.Pin_0
